# Fritzing sketch simple_encoder_reader (saved by Fritzing 0.9.6b)

parts:
  DC_Mot_Enc2 = DC Motor with two-phase hall-encoder [part_number=VT-E-G25A-06-177E]
  L298N2 = L298N DC motor driver
  U2 = LIPO-2000mAh [package=lipo-2000]
  J1 = XT60 Connector male [package=THT]  # not connected
  J2 = XT60 Connector female [package=THT]
  Part1 = Arduino Nano (Rev3.0)

nets:
  N1: DC_Mot_Enc2.pin1, L298N2.OUT2
  N2: DC_Mot_Enc2.pin3, Part1.D4
  N3: DC_Mot_Enc2.pin4, Part1.D2
  N4: DC_Mot_Enc2.pin5, Part1.3V3
  N5: DC_Mot_Enc2.pin6, L298N2.OUT1
  N6: L298N2.ENA, Part1.D9
  N7: L298N2.IN1, Part1.D12/MISO
  N8: L298N2.IN2, Part1.D13/SCK
  N9: U2.+, J2.VCC
  N10: U2.-, J2.GND

custom parts:
  L298N DC motor driver: 2x DC motor driver with 78M05 positive voltage regulator (7..35 V) L298N: max 46 V, 2 A Set 5 V Enable jumper to enable 5 V regultor (needed for the L298N) and +5 V output at screw terminal or supply external +5 V at screw terminal Set ENA and/or ENB to +5 V to enable motor permanently or supply ENA and/or ENB with PWM signal IN1 and IN2 set rotation directory for motor A (OUT1/OUT2) IN2 and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
  XT60 Connector male: Yellow XT60 connector for high current loads up to 40A male
  XT60 Connector female: Yellow XT60 connector for high current loads up to 40A female
